# Fritzing sketch Sketch (saved by Fritzing 0.9.3b)
circuit board: 8.32626cm x 5.61636cm

parts:
  Arduino = Arduino Pro Mini v13
  AMS1117 = Voltage Regulator AMS1117 [package=sot223]
  NRF24 = NRF24L01+ Breakout Board
  VCC1 = 4 x AAA Battery Mount
  JOY2 = Thumb Joystick
  JOY1 = Thumb Joystick
  PIEZO = Piezo Speaker
  Squix1 = OLED 0.96" 128x64 I2C SSD1306
  S1 = Toggle Switch [package=THT]
  LED1 = LED - 5mm [color="Red (635nm)" package="5 mm [THT]"]
  R1 = Resistor [tolerance=±5% resistance=150 package=THT]
  LED2 = LED - 5mm [color="Blue (525nm)" package="5 mm [THT]"]
  C1 = Electrolytic Capacitor [capacitance=47µF voltage=16V package="300 mil [THT, electrolytic]"]

nets:
  VCC: Arduino.VCC, AMS1117.OUT, NRF24.VCC, JOY2.VCC, JOY1.VCC, Squix1.VCC, C1.+
  N1: Arduino.A4, Squix1.SCA
  N2: Arduino.A5, Squix1.SCL
  GND: Arduino.GND, AMS1117.GND, NRF24.GND, VCC1.-, JOY2.GND, JOY1.GND, LED1.cathode, LED2.cathode
  N3: Arduino.A3, JOY1.VERT
  N4: Arduino.A2, JOY1.HORZ
  N5: Arduino.A1, JOY2.HORZ
  N6: Arduino.A0, JOY2.VERT
  N7: Arduino.D13/SCK, NRF24.SCK
  N8: Arduino.D12/MISO, NRF24.MISO
  N9: Arduino.D11_PWM/MOSI, NRF24.MOSI
  N10: Arduino.D10_PWM/SS, NRF24.CS
  N11: Arduino.D9_PWM, NRF24.CE
  N12: Arduino.D5_PWM, LED2.anode
  N13: Arduino.D4, JOY1.SEL
  N14: Arduino.D3_PWM, PIEZO.pin2
  N15: Arduino.D2, JOY2.SEL
  N16: AMS1117.IN, S1.L2, R1.Pin_0
  N17: VCC1.+, S1.COM
  N18: Squix1.GND, C1.-
  N19: LED1.anode, R1.Pin_1
