# Fritzing sketch 2Motors (saved by Fritzing 0.9.3b)
circuit board: 10cm x 8.36cm

parts:
  ARDUINO = Arduino Pro Mini v13
  FTDI = FTDI Basic Programmer
  Q1 = Basic FET N-Channel [package="TO220 [THT]"]
  Q2 = Basic FET P-Channel [package="TO220 [THT]"]
  Q3 = Basic FET N-Channel [package="TO220 [THT]"]
  Q4 = Basic FET P-Channel [package="TO220 [THT]"]
  R1 = Resistor [tolerance=±5% resistance=47 package=THT]
  R2 = Resistor [tolerance=±5% resistance=47 package=THT]
  C1 = Electrolytic Capacitor [capacitance=47µF voltage=20V package="300 mil [THT, electrolytic]"]
  R3 = Resistor [tolerance=±5% resistance=1k package=THT]
  R4 = Resistor [tolerance=±5% resistance=1k package=THT]
  SW1 = SWITCH-SPST-2 [package=switch-spst-vertical]
  C2 = Electrolytic Capacitor [capacitance=47µF voltage=20V package="300 mil [THT, electrolytic]"]
  NRF24 = NRF24L01+ Breakout Board
  Fuse1 = Fuse with Handler [part_number=Htc-15m]
  M1 = DC Motor
  Q9 = NPN-Transistor [package="TO92 [THT]"]
  LED_BACK1 = LED - 5mm [color="Red (633nm)" package="5 mm [THT]"]
  LED_BACK2 = LED - 5mm [color="Red (633nm)" package="5 mm [THT]"]
  LED_FRONT2 = LED - 5mm [color="White (4500K)" package="5 mm [THT]"]
  Q10 = NPN-Transistor [package="TO92 [THT]"]
  LED_FRONT1 = LED - 5mm [color="White (4500K)" package="5 mm [THT]"]
  LED_TOP1 = LED - 5mm [color="Blue (430nm)" package="5 mm [THT]"]
  LED_TOP2 = LED - 5mm [color="Blue (430nm)" package="5 mm [THT]"]
  Q11 = NPN-Transistor [package="TO92 [THT]"]
  Q12 = NPN-Transistor [package="TO92 [THT]"]
  BAT2 = Battery Holders [package=lipo-1100mAh]
  CHG = screw terminal, 3 pins
  IC1 = Voltage Regulator AMS1117 [package=sot223]
  BAT1 = Battery Holders [package=lipo-1100mAh]
  PIEZO = Piezo Speaker
  LED_STAT1 = LED - 3mm [color="Green (555nm)" package="3 mm [THT]"]
  R5 = Resistor [tolerance=±5% resistance=47 package=THT]
  LED_PROG1 = LED - 3mm [color="Red (633nm)" package="3 mm [THT]"]
  Q13 = Basic FET N-Channel [package="TO220 [THT]"]
  Q14 = Basic FET N-Channel [package="TO220 [THT]"]
  Q15 = Basic FET P-Channel [package="TO220 [THT]"]
  Q16 = Basic FET P-Channel [package="TO220 [THT]"]
  R6 = Resistor [tolerance=±5% resistance=1k package=THT]
  R7 = Resistor [tolerance=±5% resistance=1k package=THT]
  R8 = Resistor [tolerance=±5% resistance=47 package=THT]
  R9 = Resistor [tolerance=±5% resistance=47 package=THT]
  M2 = DC Motor

nets:
  N1: ARDUINO.DTR, FTDI.DTR
  N2: ARDUINO.D0/TX, FTDI.RXI
  N3: ARDUINO.D1/RX, FTDI.TXO
  VCC: ARDUINO.VCC, C1.+, NRF24.VCC, LED_BACK1.anode, LED_BACK2.anode, LED_FRONT2.anode, LED_FRONT1.anode, LED_TOP1.anode, LED_TOP2.anode, IC1.OUT
  GND: ARDUINO.GND, FTDI.CTS, FTDI.GND, Q1.source, Q3.source, C1.-, R3.Pin_0, R4.Pin_0, C2.-, NRF24.GND, Q9.C, Q10.C, Q11.C, Q12.C, BAT2.-, CHG.pin1, IC1.GND, PIEZO.pin1, LED_STAT1.cathode, LED_PROG1.cathode, Q13.source, Q14.source, R6.Pin_0, R7.Pin_0
  N4: ARDUINO.A3, Q12.B
  N5: ARDUINO.A2, Q11.B
  N6: ARDUINO.A1, Q10.B
  N7: ARDUINO.A0, Q9.B
  N8: ARDUINO.D13/SCK, NRF24.SCK
  N9: ARDUINO.D12/MISO, NRF24.MISO
  N10: ARDUINO.D11_PWM/MOSI, NRF24.MOSI
  N11: ARDUINO.D10_PWM/SS, NRF24.CS
  N12: ARDUINO.D9_PWM, NRF24.CE
  N13: ARDUINO.D8, R9.Pin_1
  N14: ARDUINO.D7, R2.Pin_1
  N15: ARDUINO.D6_PWM, R8.Pin_0
  N16: ARDUINO.D5_PWM, R1.Pin_0
  N17: ARDUINO.D4, LED_STAT1.anode
  N18: ARDUINO.D3_PWM, PIEZO.pin2
  N19: FTDI.POWER, R5.Pin_0
  N20: Q1.gate, Q2.gate, R2.Pin_0, R4.Pin_1
  N21: Q1.drain, Q2.source, M1.pin_1
  N22: Q2.drain, Q4.drain, SW1.P, C2.+, IC1.IN, Q15.drain, Q16.drain
  N23: Q3.gate, Q4.gate, R1.Pin_1, R3.Pin_1
  N24: Q3.drain, Q4.source, M1.pin_2
  N25: SW1.O, Fuse1.Connector2
  N26: Fuse1.Connector1, CHG.pin3, BAT1.+
  N27: Q9.E, LED_BACK1.cathode, LED_BACK2.cathode
  N28: LED_FRONT2.cathode, Q10.E, LED_FRONT1.cathode
  N29: LED_TOP1.cathode, Q11.E
  N30: LED_TOP2.cathode, Q12.E
  N31: BAT2.+, CHG.pin2, BAT1.-
  N32: R5.Pin_1, LED_PROG1.anode
  N33: Q13.gate, Q15.gate, R7.Pin_1, R8.Pin_1
  N34: Q13.drain, Q15.source, M2.pin_2
  N35: Q14.gate, Q16.gate, R6.Pin_1, R9.Pin_0
  N36: Q14.drain, Q16.source, M2.pin_1

notes:
  USE P-CH: FQP27P06
  USE N-CH: PSMN022-30PL,127
  ALL PNP&NPN = EBC
  -
